# Fritzing sketch connection_schematics (saved by Fritzing 0.9.3b)
breadboards: 1

parts:
  Raspberry_Pi_1 = Raspberry Pi 3 [part_number=RPI-3-V1.2]
  VCC1 = 4 x AAA Battery Mount
  S2 = Toggle Switch [package=THT]
  Part1 = Thermal Printer

nets:
  N1: Raspberry_Pi_1.GIPO15, Part1.TXD
  N2: VCC1.+, Part1.VH
  N3: S2.COM, Part1.GND#0
